// Logisim project decode.circ as structural Verilog: 1 circuit, main circuit main
module main (
  input  [6:0] in_1,
  input  [6:0] in_2,
  input  [2:0] in_3,
  input  [4:0] in_4,
  input  [31:0] in_5,
  input  [4:0] in_6,
  input  [6:0] in_7,
  input  [6:0] in_8,
  input  in_9
);

  wire comparator_1_eq, comparator_2_eq;
  wire [6:0] undriven;
  wire [7:1] undriven_2;

  Comparator #(.width(7)) comparator_1 (.a(undriven), .b(in_8), .eq(comparator_1_eq));  // open: gt, lt
  Comparator comparator_2 (.b({undriven_2, in_9}), .eq(comparator_2_eq));  // open: a, gt, lt
  // Pins of 1 and 8 bits meet at {undriven_2, in_9}
endmodule
