// Logisim project i type.circ as structural Verilog: 1 circuit, main circuit main
module main (
  input  [6:0] in_1,
  output lui,
  output jal,
  output r_format,
  output branch,
  output i_type,
  output load,
  output jalr,
  output store
);

  Comparator #(.width(7)) comparator_1 (.a(7'b0110111), .b(in_1), .eq(lui));  // open: gt, lt
  Comparator #(.width(7)) comparator_2 (.a(7'b1101111), .b(in_1), .eq(jal));  // open: gt, lt
  Comparator #(.width(7)) comparator_3 (.a(7'b0110011), .b(in_1), .eq(r_format));  // open: gt, lt
  Comparator #(.width(7)) comparator_4 (.a(7'b1100011), .b(in_1), .eq(branch));  // open: gt, lt
  Comparator #(.width(7)) comparator_5 (.a(7'b0010011), .b(in_1), .eq(i_type));  // open: gt, lt
  Comparator #(.width(7)) comparator_6 (.a(7'b0000011), .b(in_1), .eq(load));  // open: gt, lt
  Comparator #(.width(7)) comparator_7 (.a(7'b1100111), .b(in_1), .eq(jalr));  // open: gt, lt
  Comparator #(.width(7)) comparator_8 (.a(7'b0100011), .b(in_1), .eq(store));  // open: gt, lt
endmodule
