// Logisim project singlecycle.circ as structural Verilog: 10 circuits, main circuit main
module main (
);

  wire branch_operation_1_out_5, clock_1_out, control_decode_1_out_6, instruction_decoder_1_out_2,
       instruction_decoder_1_out_3, instruction_decoder_1_out_4, instruction_decoder_1_out_5,
       instruction_decoder_1_out_6, not_1_out, or_1_out, or_2_out;
  wire [2:0] control_decode_1_out_5;
  wire [4:0] control_decode_1_out_2, control_decode_1_out_3, control_decode_1_out_4;
  wire [11:0] load_operation_1_out_6, multiplexer_3_out, store_operation_1_out_6;
  wire [31:0] adder_1_out, alu_1_out_6, immediate_generator_1_i_immediate, immediate_generator_1_s_immediate,
       immediate_generator_1_sb_immediate, load_operation_1_out_7, multiplexer_1_out, multiplexer_2_out,
       multiplexer_4_out, ram_1_data, register_1_q, register_file_1_out_6, register_file_1_out_7, rom_1_data,
       store_operation_1_out_7;

  Clock clock_1 (.out(clock_1_out));
  Multiplexer #(.width(32), .enable("false")) multiplexer_1 (
    .in0(adder_1_out), .in1(immediate_generator_1_sb_immediate), .out(multiplexer_1_out),
    .sel(branch_operation_1_out_5));
  Register #(.width(32)) register_1 (.D(multiplexer_1_out), .Q(register_1_q), .clk(clock_1_out));  // open: en, clr
  Adder #(.width(32)) adder_1 (.a(32'h4), .b(register_1_q), .out(adder_1_out));  // open: cin, cout
  // Probe on adder_1_out
  ROM #(.addrWidth(10), .dataWidth(32)) rom_1 (.addr(register_1_q[11:2]), .data(rom_1_data));  // open: sel
  // Probe on control_decode_1_out_2
  // Probe on control_decode_1_out_3
  // Probe on control_decode_1_out_4
  Branch_Operation branch_operation_1 (
    .RS_1(register_file_1_out_6), .RS_2(register_file_1_out_7), .Function_3(control_decode_1_out_5),
    .Enable(instruction_decoder_1_out_6), .out_5(branch_operation_1_out_5));
  // Probe on multiplexer_4_out
  Control_Decode control_decode_1 (
    .in_1(rom_1_data), .out_5(control_decode_1_out_5), .out_6(control_decode_1_out_6),
    .out_2(control_decode_1_out_2), .out_3(control_decode_1_out_3), .out_4(control_decode_1_out_4));
  Instruction_Decoder instruction_decoder_1 (
    .in_1(rom_1_data), .out_2(instruction_decoder_1_out_2), .out_3(instruction_decoder_1_out_3),
    .out_4(instruction_decoder_1_out_4), .out_5(instruction_decoder_1_out_5),
    .out_6(instruction_decoder_1_out_6));
  Immediate_Generator immediate_generator_1 (
    .I_Immediate(immediate_generator_1_i_immediate), .Instruction(rom_1_data),
    .S_immediate(immediate_generator_1_s_immediate), .Program_Counter(register_1_q),
    .SB_Immediate(immediate_generator_1_sb_immediate));
  Register_File register_file_1 (
    .in_1(multiplexer_4_out), .in_2(control_decode_1_out_2), .in_3(clock_1_out),
    .in_4(control_decode_1_out_3), .in_5(control_decode_1_out_4), .out_6(register_file_1_out_6),
    .out_7(register_file_1_out_7));
  or or_1 (or_1_out, instruction_decoder_1_out_3, instruction_decoder_1_out_5);
  LOAD_Operation load_operation_1 (
    .in_2(immediate_generator_1_i_immediate), .in_3(ram_1_data), .in_4(control_decode_1_out_5),
    .out_6(load_operation_1_out_6), .out_7(load_operation_1_out_7), .in_5(instruction_decoder_1_out_2),
    .in_1(control_decode_1_out_3));
  STORE_Operation store_operation_1 (
    .in_2(immediate_generator_1_s_immediate), .in_3(register_file_1_out_7), .in_4(control_decode_1_out_5),
    .out_6(store_operation_1_out_6), .out_7(store_operation_1_out_7), .in_5(instruction_decoder_1_out_4),
    .in_1(control_decode_1_out_3));
  ALU alu_1 (
    .in_1(register_file_1_out_6), .in_2(multiplexer_2_out), .in_3(control_decode_1_out_5),
    .in_4(control_decode_1_out_6), .in_5(or_1_out), .out_6(alu_1_out_6));
  or or_2 (or_2_out, instruction_decoder_1_out_2, instruction_decoder_1_out_4);
  // Probe on store_operation_1_out_7
  // Probe on register_file_1_out_6
  // Probe on register_file_1_out_7
  Multiplexer #(.width(32), .enable("false")) multiplexer_2 (
    .in0(immediate_generator_1_i_immediate), .in1(register_file_1_out_7), .out(multiplexer_2_out),
    .sel(instruction_decoder_1_out_5));
  // Probe on multiplexer_3_out
  Multiplexer #(.width(12)) multiplexer_3 (
    .in0(load_operation_1_out_6), .in1(store_operation_1_out_6), .out(multiplexer_3_out),
    .sel(instruction_decoder_1_out_4), .en(or_2_out));
  not not_1 (not_1_out, clock_1_out);
  Multiplexer #(.width(32), .enable("false")) multiplexer_4 (
    .in0(alu_1_out_6), .in1(load_operation_1_out_7), .out(multiplexer_4_out),
    .sel(instruction_decoder_1_out_2));
  RAM #(.addrWidth(12), .dataWidth(32), .bus("separate")) ram_1 (
    .addr(multiplexer_3_out), .din(store_operation_1_out_7), .data(ram_1_data),
    .str(instruction_decoder_1_out_4), .clk(not_1_out), .ld(instruction_decoder_1_out_2));  // open: sel, clr
  // Probe on ram_1_data

  // Notes on the sheet:
  //   contents of rom_1 (hex, n*v repeats v):
  //   0 93 100113 1400213 2081b3 2000b3 300133 fff20213 fe0218e3 30a023
endmodule

module _4_Registers (
  input  [31:0] in_1,
  input  in_2,
  input  in_3,
  input  in_4,
  input  in_5,
  input  in_6,
  output [31:0] out_7,
  output [31:0] out_8,
  output [31:0] out_9,
  output [31:0] out_10
);

  Register #(.width(32)) register_1 (.D(in_1), .en(in_2), .Q(out_7), .clk(in_6));  // open: clr
  Register #(.width(32)) register_2 (.D(in_1), .en(in_4), .Q(out_9), .clk(in_6));  // open: clr
  Register #(.width(32)) register_3 (.D(in_1), .en(in_3), .Q(out_8), .clk(in_6));  // open: clr
  Register #(.width(32)) register_4 (.D(in_1), .en(in_5), .Q(out_10), .clk(in_6));  // open: clr
endmodule

module Register_File (
  input  [31:0] in_1,
  input  [4:0] in_2,
  input  in_3,
  input  [4:0] in_4,
  input  [4:0] in_5,
  output [31:0] out_6,
  output [31:0] out_7
);

  wire decoder_1_out0, decoder_1_out1, decoder_1_out2, decoder_1_out3, decoder_1_out4, decoder_1_out5,
       decoder_1_out6, decoder_1_out7, decoder_1_out8, decoder_1_out9, decoder_1_out10, decoder_1_out11,
       decoder_1_out12, decoder_1_out13, decoder_1_out14, decoder_1_out15, decoder_1_out16, decoder_1_out17,
       decoder_1_out18, decoder_1_out19, decoder_1_out20, decoder_1_out21, decoder_1_out22, decoder_1_out23,
       decoder_1_out24, decoder_1_out25, decoder_1_out26, decoder_1_out27, decoder_1_out28, decoder_1_out29,
       decoder_1_out30, decoder_1_out31;
  wire [31:0] n4_registers_1_out_7, n4_registers_1_out_8, n4_registers_1_out_9, n4_registers_1_out_10,
       n4_registers_2_out_7, n4_registers_2_out_8, n4_registers_2_out_9, n4_registers_2_out_10,
       n4_registers_3_out_7, n4_registers_3_out_8, n4_registers_3_out_9, n4_registers_3_out_10,
       n4_registers_4_out_7, n4_registers_4_out_8, n4_registers_4_out_9, n4_registers_4_out_10,
       n4_registers_5_out_7, n4_registers_5_out_8, n4_registers_5_out_9, n4_registers_5_out_10,
       n4_registers_6_out_7, n4_registers_6_out_8, n4_registers_6_out_9, n4_registers_6_out_10,
       n4_registers_7_out_7, n4_registers_7_out_8, n4_registers_7_out_9, n4_registers_7_out_10,
       n4_registers_8_out_7, n4_registers_8_out_8, n4_registers_8_out_9, n4_registers_8_out_10;

  Decoder #(.select(5), .enable("false")) decoder_1 (
    .out0(decoder_1_out0), .out1(decoder_1_out1), .out2(decoder_1_out2), .out3(decoder_1_out3),
    .out4(decoder_1_out4), .out5(decoder_1_out5), .out6(decoder_1_out6), .out7(decoder_1_out7),
    .out8(decoder_1_out8), .out9(decoder_1_out9), .out10(decoder_1_out10), .out11(decoder_1_out11),
    .out12(decoder_1_out12), .out13(decoder_1_out13), .out14(decoder_1_out14), .out15(decoder_1_out15),
    .out16(decoder_1_out16), .out17(decoder_1_out17), .out18(decoder_1_out18), .out19(decoder_1_out19),
    .out20(decoder_1_out20), .out21(decoder_1_out21), .out22(decoder_1_out22), .out23(decoder_1_out23),
    .out24(decoder_1_out24), .out25(decoder_1_out25), .out26(decoder_1_out26), .out27(decoder_1_out27),
    .out28(decoder_1_out28), .out29(decoder_1_out29), .out30(decoder_1_out30), .out31(decoder_1_out31),
    .sel(in_2));
  _4_Registers u_4_registers_1 (
    .in_1(in_1), .in_2(decoder_1_out0), .in_3(decoder_1_out1), .in_4(decoder_1_out2), .in_5(decoder_1_out3),
    .in_6(in_3), .out_7(n4_registers_1_out_7), .out_8(n4_registers_1_out_8), .out_9(n4_registers_1_out_9),
    .out_10(n4_registers_1_out_10));
  _4_Registers u_4_registers_2 (
    .in_1(in_1), .in_2(decoder_1_out4), .in_3(decoder_1_out5), .in_4(decoder_1_out6), .in_5(decoder_1_out7),
    .in_6(in_3), .out_7(n4_registers_2_out_7), .out_8(n4_registers_2_out_8), .out_9(n4_registers_2_out_9),
    .out_10(n4_registers_2_out_10));
  _4_Registers u_4_registers_3 (
    .in_1(in_1), .in_2(decoder_1_out8), .in_3(decoder_1_out9), .in_4(decoder_1_out10),
    .in_5(decoder_1_out11), .in_6(in_3), .out_7(n4_registers_3_out_7), .out_8(n4_registers_3_out_8),
    .out_9(n4_registers_3_out_9), .out_10(n4_registers_3_out_10));
  _4_Registers u_4_registers_4 (
    .in_1(in_1), .in_2(decoder_1_out12), .in_3(decoder_1_out13), .in_4(decoder_1_out14),
    .in_5(decoder_1_out15), .in_6(in_3), .out_7(n4_registers_4_out_7), .out_8(n4_registers_4_out_8),
    .out_9(n4_registers_4_out_9), .out_10(n4_registers_4_out_10));
  _4_Registers u_4_registers_5 (
    .in_1(in_1), .in_2(decoder_1_out16), .in_3(decoder_1_out17), .in_4(decoder_1_out18),
    .in_5(decoder_1_out19), .in_6(in_3), .out_7(n4_registers_5_out_7), .out_8(n4_registers_5_out_8),
    .out_9(n4_registers_5_out_9), .out_10(n4_registers_5_out_10));
  _4_Registers u_4_registers_6 (
    .in_1(in_1), .in_2(decoder_1_out20), .in_3(decoder_1_out21), .in_4(decoder_1_out22),
    .in_5(decoder_1_out23), .in_6(in_3), .out_7(n4_registers_6_out_7), .out_8(n4_registers_6_out_8),
    .out_9(n4_registers_6_out_9), .out_10(n4_registers_6_out_10));
  _4_Registers u_4_registers_7 (
    .in_1(in_1), .in_2(decoder_1_out24), .in_3(decoder_1_out25), .in_4(decoder_1_out26),
    .in_5(decoder_1_out27), .in_6(in_3), .out_7(n4_registers_7_out_7), .out_8(n4_registers_7_out_8),
    .out_9(n4_registers_7_out_9), .out_10(n4_registers_7_out_10));
  _4_Registers u_4_registers_8 (
    .in_1(in_1), .in_2(decoder_1_out28), .in_3(decoder_1_out29), .in_4(decoder_1_out30),
    .in_5(decoder_1_out31), .in_6(in_3), .out_7(n4_registers_8_out_7), .out_8(n4_registers_8_out_8),
    .out_9(n4_registers_8_out_9), .out_10(n4_registers_8_out_10));
  Multiplexer #(.select(5), .width(32), .enable("false")) multiplexer_1 (
    .in0(n4_registers_1_out_7), .in1(n4_registers_1_out_8), .in2(n4_registers_1_out_9),
    .in3(n4_registers_1_out_10), .in4(n4_registers_2_out_7), .in5(n4_registers_2_out_8),
    .in6(n4_registers_2_out_9), .in7(n4_registers_2_out_10), .in8(n4_registers_3_out_7),
    .in9(n4_registers_3_out_8), .in10(n4_registers_3_out_9), .in11(n4_registers_3_out_10),
    .in12(n4_registers_4_out_7), .in13(n4_registers_4_out_8), .in14(n4_registers_4_out_9),
    .in15(n4_registers_4_out_10), .in16(n4_registers_5_out_7), .in17(n4_registers_5_out_8),
    .in18(n4_registers_5_out_9), .in19(n4_registers_5_out_10), .in20(n4_registers_6_out_7),
    .in21(n4_registers_6_out_8), .in22(n4_registers_6_out_9), .in23(n4_registers_6_out_10),
    .in24(n4_registers_7_out_7), .in25(n4_registers_7_out_8), .in26(n4_registers_7_out_9),
    .in27(n4_registers_7_out_10), .in28(n4_registers_8_out_7), .in29(n4_registers_8_out_8),
    .in30(n4_registers_8_out_9), .in31(n4_registers_8_out_10), .out(out_6), .sel(in_4));
  Multiplexer #(.select(5), .width(32), .enable("false")) multiplexer_2 (
    .in0(n4_registers_1_out_7), .in1(n4_registers_1_out_8), .in2(n4_registers_1_out_9),
    .in3(n4_registers_1_out_10), .in4(n4_registers_2_out_7), .in5(n4_registers_2_out_8),
    .in6(n4_registers_2_out_9), .in7(n4_registers_2_out_10), .in8(n4_registers_3_out_7),
    .in9(n4_registers_3_out_8), .in10(n4_registers_3_out_9), .in11(n4_registers_3_out_10),
    .in12(n4_registers_4_out_7), .in13(n4_registers_4_out_8), .in14(n4_registers_4_out_9),
    .in15(n4_registers_4_out_10), .in16(n4_registers_5_out_7), .in17(n4_registers_5_out_8),
    .in18(n4_registers_5_out_9), .in19(n4_registers_5_out_10), .in20(n4_registers_6_out_7),
    .in21(n4_registers_6_out_8), .in22(n4_registers_6_out_9), .in23(n4_registers_6_out_10),
    .in24(n4_registers_7_out_7), .in25(n4_registers_7_out_8), .in26(n4_registers_7_out_9),
    .in27(n4_registers_7_out_10), .in28(n4_registers_8_out_7), .in29(n4_registers_8_out_8),
    .in30(n4_registers_8_out_9), .in31(n4_registers_8_out_10), .out(out_7), .sel(in_5));
endmodule

module Immediate_Generator (
  input  [31:0] Instruction,
  input  [31:0] Program_Counter,
  output [31:0] I_Immediate,
  output [31:0] S_immediate,
  output [31:0] SB_Immediate
);

  wire [31:0] bit_extender_3_out;

  assign I_Immediate = {{20{Instruction[31]}}, Instruction[31:20]};  // Bit_Extender bit_extender_1
  assign S_immediate = {{20{1'b0}}, {Instruction[31:25], Instruction[11:7]}};  // Bit_Extender bit_extender_2
  assign bit_extender_3_out = {{19{1'b0}}, {Instruction[31], Instruction[7], Instruction[30:25], Instruction[11:8], 1'b0}};  // Bit_Extender bit_extender_3
  Adder #(.width(32)) adder_1 (.a(bit_extender_3_out), .b(Program_Counter), .out(SB_Immediate));  // open: cin, cout
endmodule

module Instruction_Decoder (
  input  [31:0] in_1,
  output out_2,
  output out_3,
  output out_4,
  output out_5,
  output out_6
);

  Comparator #(.width(7), .mode("unsigned")) comparator_1 (.a(7'b0000011), .b(in_1[6:0]), .eq(out_2));  // open: gt, lt
  Comparator #(.width(7), .mode("unsigned")) comparator_2 (.a(7'b0010011), .b(in_1[6:0]), .eq(out_3));  // open: gt, lt
  Comparator #(.width(7), .mode("unsigned")) comparator_3 (.a(7'b0100011), .b(in_1[6:0]), .eq(out_4));  // open: gt, lt
  Comparator #(.width(7), .mode("unsigned")) comparator_4 (.a(7'b0110011), .b(in_1[6:0]), .eq(out_5));  // open: gt, lt
  Comparator #(.width(7), .mode("unsigned")) comparator_5 (.a(7'b1100011), .b(in_1[6:0]), .eq(out_6));  // open: gt, lt
endmodule

module ALU (
  input  [31:0] in_1,
  input  [31:0] in_2,
  input  [2:0] in_3,
  input  in_4,
  input  in_5,
  output [31:0] out_6
);

  wire comparator_1_lt, comparator_2_lt;
  wire [31:0] adder_1_out, and_1_out, multiplexer_1_out, multiplexer_2_out, multiplexer_3_out,
       multiplexer_4_out, or_1_out, shifter_1_out, shifter_2_out, shifter_3_out, subtractor_1_out, xor_1_out;

  Adder #(.width(32)) adder_1 (.a(in_1), .b(in_2), .out(adder_1_out));  // open: cin, cout
  Subtractor #(.width(32)) subtractor_1 (.a(in_1), .b(in_2), .out(subtractor_1_out));  // open: bin, bout
  Shifter #(.width(32)) shifter_1 (.in(in_1), .\dist (in_2[4:0]), .out(shifter_1_out));
  Comparator #(.width(32)) comparator_1 (.a(in_1), .b(in_2), .lt(comparator_1_lt));  // open: gt, eq
  Comparator #(.width(32)) comparator_2 (.a(in_1), .b(in_2), .lt(comparator_2_lt));  // open: gt, eq
  assign xor_1_out = in_1 ^ in_2;  // XOR_Gate xor_1, 32 bits wide
  Shifter #(.width(32), .shift("lr")) shifter_2 (.in(in_1), .\dist (in_2[4:0]), .out(shifter_2_out));
  Shifter #(.width(32), .shift("ar")) shifter_3 (.in(in_1), .\dist (in_2[4:0]), .out(shifter_3_out));
  assign or_1_out = in_1 | in_2;  // OR_Gate or_1, 32 bits wide
  assign and_1_out = in_1 & in_2;  // AND_Gate and_1, 32 bits wide
  Multiplexer #(.width(32), .enable("false")) multiplexer_1 (
    .in0({32{1'b0}}), .in1(32'h1), .out(multiplexer_1_out), .sel(comparator_1_lt));
  Multiplexer #(.width(32), .enable("false")) multiplexer_2 (
    .in0({32{1'b0}}), .in1(32'h1), .out(multiplexer_2_out), .sel(comparator_2_lt));
  Multiplexer #(.width(32), .enable("false")) multiplexer_3 (
    .in0(adder_1_out), .in1(subtractor_1_out), .out(multiplexer_3_out), .sel(in_4));
  Multiplexer #(.width(32), .enable("false")) multiplexer_4 (
    .in0(shifter_2_out), .in1(shifter_3_out), .out(multiplexer_4_out), .sel(in_4));
  Multiplexer #(.select(3), .width(32)) multiplexer_5 (
    .in0(multiplexer_3_out), .in1(shifter_1_out), .in2(multiplexer_1_out), .in3(multiplexer_2_out),
    .in4(xor_1_out), .in5(multiplexer_4_out), .in6(or_1_out), .in7(and_1_out), .out(out_6), .sel(in_3),
    .en(in_5));
endmodule

module LOAD_Operation (
  input  [4:0] in_1,
  input  [31:0] in_2,
  input  [31:0] in_3,
  input  [2:0] in_4,
  input  in_5,
  output [11:0] out_6,
  output [31:0] out_7
);

  wire [31:0] bit_extender_1_out, bit_extender_2_out, bit_extender_3_out, bit_extender_4_out,
       bit_extender_5_out;
  wire [31:12] adder_1_out;

  assign bit_extender_1_out = {{27{1'b0}}, in_1};  // Bit_Extender bit_extender_1
  assign bit_extender_2_out = {{24{in_3[7]}}, in_3[7:0]};  // Bit_Extender bit_extender_2
  assign bit_extender_3_out = {{16{in_3[15]}}, in_3[15:0]};  // Bit_Extender bit_extender_3
  assign bit_extender_4_out = {{24{1'b0}}, in_3[7:0]};  // Bit_Extender bit_extender_4
  assign bit_extender_5_out = {{16{1'b0}}, in_3[15:0]};  // Bit_Extender bit_extender_5
  Adder #(.width(32)) adder_1 (.a(bit_extender_1_out), .b(in_2), .out({adder_1_out, out_6}));  // open: cin, cout
  Multiplexer #(.select(3), .width(32)) multiplexer_1 (
    .in0(bit_extender_2_out), .in1(bit_extender_3_out), .in2(in_3), .in4(bit_extender_4_out),
    .in5(bit_extender_5_out), .out(out_7), .sel(in_4), .en(in_5));  // open: in3, in6, in7
endmodule

module STORE_Operation (
  input  [4:0] in_1,
  input  [31:0] in_2,
  input  [31:0] in_3,
  input  [2:0] in_4,
  input  in_5,
  output [11:0] out_6,
  output [31:0] out_7
);

  wire [31:0] bit_extender_1_out, bit_extender_2_out, bit_extender_3_out;
  wire [31:12] adder_1_out;

  assign bit_extender_1_out = {{27{1'b0}}, in_1};  // Bit_Extender bit_extender_1
  assign bit_extender_2_out = {{24{in_3[7]}}, in_3[7:0]};  // Bit_Extender bit_extender_2
  assign bit_extender_3_out = {{16{in_3[15]}}, in_3[15:0]};  // Bit_Extender bit_extender_3
  Adder #(.width(32)) adder_1 (.a(bit_extender_1_out), .b(in_2), .out({adder_1_out, out_6}));  // open: cin, cout
  Multiplexer #(.select(3), .width(32)) multiplexer_1 (
    .in0(bit_extender_2_out), .in1(bit_extender_3_out), .in2(in_3), .out(out_7), .sel(in_4), .en(in_5));  // open: in3, in4, in5, in6, in7
endmodule

module Control_Decode (
  input  [31:0] in_1,
  output [4:0] out_2,
  output [4:0] out_3,
  output [4:0] out_4,
  output [2:0] out_5,
  output out_6
);

  wire and_1_out, comparator_1_eq, comparator_2_eq, comparator_3_eq, multiplexer_1_out;

  Comparator #(.width(7), .mode("unsigned")) comparator_1 (
    .a(7'b0110011), .b(in_1[6:0]), .eq(comparator_1_eq));  // open: gt, lt
  Comparator #(.width(7), .mode("unsigned")) comparator_2 (
    .a(7'b0010011), .b(in_1[6:0]), .eq(comparator_2_eq));  // open: gt, lt
  Comparator #(.width(3)) comparator_3 (.a(in_1[14:12]), .b(3'b101), .eq(comparator_3_eq));  // open: gt, lt
  and and_1 (and_1_out, comparator_3_eq, comparator_2_eq);
  Multiplexer #(.enable("false")) multiplexer_1 (
    .in0(1'b0), .in1(in_1[30]), .out(multiplexer_1_out), .sel(comparator_1_eq));
  Multiplexer #(.enable("false")) multiplexer_2 (.in0(multiplexer_1_out), .in1(in_1[30]), .out(out_6), .sel(and_1_out));

  assign out_2 = in_1[11:7];
  assign out_3 = in_1[19:15];
  assign out_4 = in_1[24:20];
  assign out_5 = in_1[14:12];
endmodule

module Branch_Operation (
  input  [31:0] RS_1,
  input  [31:0] RS_2,
  input  [2:0] Function_3,
  input  Enable,
  output out_5
);

  wire comparator_1_eq, comparator_2_gt, comparator_2_lt, comparator_3_lt, comparator_4_gt, comparator_5_lt,
       comparator_6_gt, multiplexer_1_out, or_1_out;

  Comparator #(.width(32)) comparator_1 (.a(RS_1), .b(RS_2), .eq(comparator_1_eq));  // open: gt, lt
  Comparator #(.width(32)) comparator_2 (.a(RS_1), .b(RS_2), .gt(comparator_2_gt), .lt(comparator_2_lt));  // open: eq
  Comparator #(.width(32)) comparator_3 (.a(RS_1), .b(RS_2), .lt(comparator_3_lt));  // open: gt, eq
  Comparator #(.width(32)) comparator_4 (.a(RS_1), .b(RS_2), .gt(comparator_4_gt));  // open: eq, lt
  Comparator #(.width(32), .mode("unsigned")) comparator_5 (.a(RS_1), .b(RS_2), .lt(comparator_5_lt));  // open: gt, eq
  Comparator #(.width(32), .mode("unsigned")) comparator_6 (.a(RS_1), .b(RS_2), .gt(comparator_6_gt));  // open: eq, lt
  or or_1 (or_1_out, comparator_2_gt, comparator_2_lt);
  Multiplexer #(.select(3)) multiplexer_1 (
    .in0(comparator_1_eq), .in1(or_1_out), .in4(comparator_3_lt), .in5(comparator_4_gt),
    .in6(comparator_5_lt), .in7(comparator_6_gt), .out(multiplexer_1_out), .sel(Function_3), .en(Enable));  // open: in2, in3
  Multiplexer #(.enable("false")) multiplexer_2 (.in0(1'b0), .in1(multiplexer_1_out), .out(out_5), .sel(Enable));
endmodule
